// Logisim project Physics_CPU.circ as structural Verilog: 6 circuits, main circuit main
module main (
  input  in_1
);

  wire aluRegOut, aRegLoad, aRegOut, bRegLoad, bRegOut, clock_1_out, counterOut, increment,
       instructionRegLoad, instructionRegOut, loadAddress, loadCounter, memoryOut, sub, writeMemory;
  wire [7:0] A_Register_dataout, B_Register_dataout, Instruction_Register_dataout;
  wire [7:2] eightbitcounter_1_counterout;

  Clock clock_1 (.out(clock_1_out));
  EightBitCounter eightbitcounter_1 (
    .enableOutput(counterOut), .load(loadCounter),
    .addressIn({eightbitcounter_1_counterout, {2{eightbitcounter_1_counterout[7]}}}), .increment(increment),
    .clock(clock_1_out), .reset(in_1),
    .counterOut({eightbitcounter_1_counterout, {2{eightbitcounter_1_counterout[7]}}}));
  Memory memory_1 (
    .loadAddress(loadAddress), .reset(in_1),
    .address({eightbitcounter_1_counterout, {2{eightbitcounter_1_counterout[7]}}}),
    .dataIn({eightbitcounter_1_counterout, {2{eightbitcounter_1_counterout[7]}}}), .write(writeMemory),
    .clock(clock_1_out), .enableOutput(memoryOut),
    .dataOut({eightbitcounter_1_counterout, {2{eightbitcounter_1_counterout[7]}}}));
  EightBitReg Instruction_Register (
    .clock(clock_1_out), .load(instructionRegLoad), .enableOutput(instructionRegOut), .reset(in_1),
    .dataIn({eightbitcounter_1_counterout, {2{eightbitcounter_1_counterout[7]}}}),
    .dataOut(Instruction_Register_dataout));  // open: bufferedOut
  ControlModule controlmodule_1 (
    .instruction(Instruction_Register_dataout), .flags(3'b111), .clock(clock_1_out));  // open: controlBits
  EightBitReg A_Register (
    .clock(clock_1_out), .load(aRegLoad), .enableOutput(aRegOut), .reset(in_1),
    .dataIn({eightbitcounter_1_counterout, {2{eightbitcounter_1_counterout[7]}}}),
    .bufferedOut({eightbitcounter_1_counterout, {2{eightbitcounter_1_counterout[7]}}}),
    .dataOut(A_Register_dataout));
  ALU alu_1 (
    .A(A_Register_dataout), .B(B_Register_dataout), .sub(sub), .enableOutput(aluRegOut),
    .calcOut({eightbitcounter_1_counterout, {2{eightbitcounter_1_counterout[7]}}}));
  EightBitReg B_Register (
    .clock(clock_1_out), .load(bRegLoad), .enableOutput(bRegOut), .reset(in_1),
    .dataIn({eightbitcounter_1_counterout, {2{eightbitcounter_1_counterout[7]}}}),
    .bufferedOut({eightbitcounter_1_counterout, {2{eightbitcounter_1_counterout[7]}}}),
    .dataOut(B_Register_dataout));

  // Other names for the same wires on the sheet: reset = in_1
endmodule

module EightBitReg (
  input  clock,
  input  load,
  input  enableOutput,
  input  reset,
  input  [7:0] dataIn,
  output [7:0] bufferedOut,
  output [7:0] dataOut
);

  Register register_1 (.D(dataIn), .en(load), .clk(clock), .Q(dataOut), .clr(reset));
  assign bufferedOut = enableOutput ? dataOut : 8'bz;  // Controlled_Buffer controlled_buffer_1
endmodule

module ALU (
  input  [7:0] A,
  input  [7:0] B,
  input  sub,
  input  enableOutput,
  output [7:0] calcOut
);

  wire [7:0] adder_1_out, xor_1_out;

  assign xor_1_out = B ^ {8{sub}};  // XOR_Gate xor_1, 8 bits wide
  Adder adder_1 (.a(A), .b(xor_1_out), .out(adder_1_out), .cin(sub));  // open: cout
  assign calcOut = enableOutput ? adder_1_out : 8'bz;  // Controlled_Buffer controlled_buffer_1
endmodule

module EightBitCounter (
  input  enableOutput,
  input  load,
  input  [7:0] addressIn,
  input  increment,
  input  clock,
  input  reset,
  output [7:0] counterOut
);

  wire and_1_out, not_1_out, or_1_out;
  wire [7:0] adder_1_out, bit_extender_1_out, multiplexer_1_out, register_1_q;

  Adder adder_1 (.a(register_1_q), .b(bit_extender_1_out), .out(adder_1_out));  // open: cin, cout
  assign bit_extender_1_out = {{7{1'b0}}, increment};  // Bit_Extender bit_extender_1
  and and_1 (and_1_out, increment, not_1_out);
  not not_1 (not_1_out, load);
  Multiplexer #(.width(8)) multiplexer_1 (.in0(addressIn), .in1(adder_1_out), .out(multiplexer_1_out), .sel(and_1_out));
  Register register_1 (.D(multiplexer_1_out), .en(or_1_out), .clk(clock), .Q(register_1_q), .clr(reset));
  or or_1 (or_1_out, load, increment);
  assign counterOut = enableOutput ? register_1_q : 8'bz;  // Controlled_Buffer controlled_buffer_1
endmodule

module Memory (
  input  loadAddress,
  input  reset,
  input  [7:0] address,
  input  [7:0] dataIn,
  input  write,
  input  clock,
  input  enableOutput,
  output [7:0] dataOut
);

  wire [7:0] ram_1_dout, register_1_q;

  Register register_1 (.D(address), .en(loadAddress), .clk(clock), .Q(register_1_q), .clr(reset));
  RAM #(.enables("line")) ram_1 (.addr(register_1_q), .we(write), .clk(clock), .din(dataIn), .dout(ram_1_dout));
  assign dataOut = enableOutput ? ram_1_dout : 8'bz;  // Controlled_Buffer controlled_buffer_1
endmodule

module ControlModule (
  input  [7:0] instruction,
  input  [2:0] flags,
  input  clock,
  output [15:0] controlBits
);

  wire [7:0] eightbitcounter_1_counterout;

  EightBitCounter eightbitcounter_1 (
    .enableOutput(1'b1), .increment(1'b1), .clock(clock), .counterOut(eightbitcounter_1_counterout));  // open: load, addressIn, reset
  ROM #(.addrWidth(15)) rom_1 (.addr({eightbitcounter_1_counterout[3:0], flags, instruction}), .data(controlBits[7:0]));
  ROM #(.addrWidth(15)) rom_2 (
    .addr({eightbitcounter_1_counterout[3:0], flags, instruction}), .data(controlBits[15:8]));

  // Notes on the sheet:
  //   contents of rom_1 (hex, n*v repeats v):
  //   10 40 2 13*0 10 40 2 13*0 10 40 2 13*0 10 40 2 13*0 10 40 2 13*0 10 40 2 13*0 10 40 2 13*0 10 40 2
  //   13*0 10 40 10 40 0 2 10*0 10 40 10 40 0 2 10*0 10 40 10 40 0 2 10*0 10 40 10 40 0 2 10*0 10 40 10 40
  //   0 2 10*0 10 40 10 40 0 2 10*0 10 40 10 40 0 2 10*0 10 40 10 40 0 2 10*0 10 40 10 40 0 8 2 9*0 10 40
  //   10 40 0 8 2 9*0 10 40 10 40 0 8 2 9*0 10 40 10 40 0 8 2 9*0 10 40 10 40 0 8 2 9*0 10 40 10 40 0 8 2
  //   9*0 10 40 10 40 0 8 2 9*0 10 40 10 40 0 8 2 9*0 10 40 10 40 8 2 10*0 10 40 10 40 8 2 10*0 10 40 10
  //   40 8 2 10*0 10 40 10 40 8 2 10*0 10 40 10 40 8 2 10*0 10 40 10 40 8 2 10*0 10 40 10 40 8 2 10*0 10
  //   40 10 40 8 2 10*0 10 40 10 40 0 c 2 9*0 10 40 10 40 0 c 2 9*0 10 40 10 40 0 c 2 9*0 10 40 10 40 0 c
  //   2 9*0 10 40 10 40 0 c 2 9*0 10 40 10 40 0 c 2 9*0 10 40 10 40 0 c 2 9*0 10 40 10 40 0 c 2 9*0 10 40
  //   10 40 8 2 10*0 10 40 10 40 8 2 10*0 10 40 10 40 8 2 10*0 10 40 10 40 8 2 10*0 10 40 10 40 8 2 10*0
  //   10 40 10 40 8 2 10*0 10 40 10 40 8 2 10*0 10 40 10 40 8 2 10*0 10 40 10 40 0 2 10*0 10 40 10 40 0 2
  //   10*0 10 40 10 40 0 2 10*0 10 40 10 40 0 2 10*0 10 40 10 40 0 2 10*0 10 40 10 40 0 2 10*0 10 40 10 40
  //   0 2 10*0 10 40 10 40 0 2 10*0 10 40 10 40 2 11*0 10 40 10 40 2 11*0 10 40 10 40 2 11*0 10 40 10 40 2
  //   11*0 10 40 10 40 2 11*0 10 40 10 40 2 11*0 10 40 10 40 2 11*0 10 40 10 40 2 11*0 10 40 10 20 2 11*0
  //   10 40 10 20 2 11*0 10 40 10 20 2 11*0 10 40 10 20 2 11*0 10 40 10 20 2 11*0 10 40 10 20 2 11*0 10 40
  //   10 20 2 11*0 10 40 10 20 2 11*0 10 40 2 13*0 10 40 2 13*0 10 40 2 13*0 10 40 2 13*0 10 40 2 13*0 10
  //   40 2 13*0 10 40 2 13*0 10 40 2 13*0 10 40 2 13*0 10 40 2 13*0 10 40 2 13*0 10 40 2 13*0 10 40 2 13*0
  //   10 40 2 13*0 10 40 2 13*0 10 40 2 13*0 10 40 2 13*0 10 40 2 13*0 10 40 2 13*0 10 40 2 13*0 10 40 2
  //   13*0 10 40 2 13*0 10 40 2 13*0 10 40 2 13*0 10 40 2 13*0 10 40 2 13*0 10 40 2 13*0 10 40 2 13*0 10
  //   40 2 13*0 10 40 2 13*0 10 40 2 13*0 10 40 2 13*0 10 40 2 13*0 10 40 2 13*0 10 40 2 13*0 10 40 2 13*0
  //   10 40 2 13*0 10 40 2 13*0 10 40 2 13*0 10 40 2 13*0 10 40 2 13*0 10 40 2 13*0 10 40 2 13*0 10 40 2
  //   13*0 10 40 2 13*0 10 40 2 13*0 10 40 2 13*0 10 40 2 13*0 10 40 2 13*0 10 40 2 13*0 10 40 2 13*0 10
  //   40 2 13*0 10 40 2 13*0 10 40 2 13*0 10 40 2 13*0 10 40 2 13*0 10 40 2 13*0 10 40 2 13*0 10 40 2 13*0
  //   10 40 2 13*0 10 40 2 13*0 10 40 2 13*0 10 40 2 13*0 10 40 2 13*0 10 40 2 13*0 10 40 2 13*0 10 40 2
  //   13*0 10 40 2 13*0 10 40 2 13*0 10 40 2 13*0 10 40 2 13*0 10 40 2 13*0 10 40 2 13*0 10 40 2 13*0 10
  //   40 2 13*0 10 40 2 13*0 10 40 2 13*0 10 40 2 13*0 10 40 2 13*0 10 40 2 13*0 10 40 2 13*0 10 40 2 13*0
  //   10 40 2 13*0 10 40 2 13*0 10 40 2 13*0 10 40 2 13*0 10 40 2 13*0 10 40 2 13*0 10 40 2 13*0 10 40 2
  //   13*0 10 40 2 13*0 10 40 2 13*0 10 40 2 13*0 10 40 2 13*0 10 40 2 13*0 10 40 2 13*0 10 40 2 13*0 10
  //   40 2 13*0 10 40 2 13*0 10 40 2 13*0 10 40 2 13*0 10 40 2 13*0 10 40 2 13*0 10 40 2 13*0 10 40 2 13*0
  //   10 40 2 13*0 10 40 2 13*0 10 40 2 13*0 10 40 2 13*0 10 40 2 13*0 10 40 2 13*0 10 40 2 13*0 10 40 2
  //   13*0 10 40 2 13*0 10 40 2 13*0 10 40 2 13*0 10 40 2 13*0 10 40 2 13*0 10 40 2 13*0 10 40 2 13*0 10
  //   40 2 13*0 10 40 2 13*0 10 40 2 13*0 10 40 2 13*0 10 40 2 13*0 10 40 2 13*0 10 40 2 13*0 10 40 2 13*0
  //   10 40 2 13*0 10 40 2 13*0 10 40 2 13*0 10 40 2 13*0 10 40 2 13*0 10 40 2 13*0 10 40 2 13*0 10 40 2
  //   13*0 10 40 2 13*0 10 40 2 13*0 10 40 2 13*0 10 40 2 13*0 10 40 2 13*0 10 40 2 13*0 10 40 2 13*0 10
  //   40 2 13*0 10 40 2 13*0 10 40 2 13*0 10 40 2 13*0 10 40 2 13*0 10 40 2 13*0 10 40 2 13*0 10 40 2 13*0
  //   10 40 2 13*0 10 40 2 13*0 10 40 2 13*0 10 40 2 13*0 10 40 2 13*0 10 40 2 13*0 10 40 2 13*0 10 40 2
  //   13*0 10 40 2 13*0 10 40 2 13*0 10 40 2 13*0 10 40 2 13*0 10 40 2 13*0 10 40 2 13*0 10 40 2 13*0 10
  //   40 2 13*0 10 40 2 13*0 10 40 2 13*0 10 40 2 13*0 10 40 2 13*0 10 40 2 13*0 10 40 2 13*0 10 40 2 13*0
  //   10 40 2 13*0 10 40 2 13*0 10 40 2 13*0 10 40 2 13*0 10 40 2 13*0 10 40 2 13*0 10 40 2 13*0 10 40 2
  //   13*0 10 40 2 13*0 10 40 2 13*0 10 40 2 13*0 10 40 2 13*0 10 40 2 13*0 10 40 2 13*0 10 40 2 13*0 10
  //   40 2 13*0 10 40 2 13*0 10 40 2 13*0 10 40 2 13*0 10 40 2 13*0 10 40 2 13*0 10 40 2 13*0 10 40 2 13*0
  //   10 40 2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
  //   contents of rom_2 (hex, n*v repeats v):
  //   8 30 14*0 8 30 14*0 8 30 14*0 8 30 14*0 8 30 14*0 8 30 14*0 8 30 14*0 8 30 14*0 8 30 8 28 24 11*0 8
  //   30 8 28 24 11*0 8 30 8 28 24 11*0 8 30 8 28 24 11*0 8 30 8 28 24 11*0 8 30 8 28 24 11*0 8 30 8 28 24
  //   11*0 8 30 8 28 24 11*0 8 30 8 28 21 4 10*0 8 30 8 28 21 4 10*0 8 30 8 28 21 4 10*0 8 30 8 28 21 4
  //   10*0 8 30 8 28 21 4 10*0 8 30 8 28 21 4 10*0 8 30 8 28 21 4 10*0 8 30 8 28 21 4 10*0 8 30 8 21 4
  //   11*0 8 30 8 21 4 11*0 8 30 8 21 4 11*0 8 30 8 21 4 11*0 8 30 8 21 4 11*0 8 30 8 21 4 11*0 8 30 8 21
  //   4 11*0 8 30 8 21 4 11*0 8 30 8 28 21 4 10*0 8 30 8 28 21 4 10*0 8 30 8 28 21 4 10*0 8 30 8 28 21 4
  //   10*0 8 30 8 28 21 4 10*0 8 30 8 28 21 4 10*0 8 30 8 28 21 4 10*0 8 30 8 28 21 4 10*0 8 30 8 21 4
  //   11*0 8 30 8 21 4 11*0 8 30 8 21 4 11*0 8 30 8 21 4 11*0 8 30 8 21 4 11*0 8 30 8 21 4 11*0 8 30 8 21
  //   4 11*0 8 30 8 21 4 11*0 8 30 8 28 42 11*0 8 30 8 28 42 11*0 8 30 8 28 42 11*0 8 30 8 28 42 11*0 8 30
  //   8 28 42 11*0 8 30 8 28 42 11*0 8 30 8 28 42 11*0 8 30 8 28 42 11*0 8 30 8 24 12*0 8 30 8 24 12*0 8
  //   30 8 24 12*0 8 30 8 24 12*0 8 30 8 24 12*0 8 30 8 24 12*0 8 30 8 24 12*0 8 30 8 24 12*0 8 30 8 20
  //   12*0 8 30 8 20 12*0 8 30 8 20 12*0 8 30 8 20 12*0 8 30 8 20 12*0 8 30 8 20 12*0 8 30 8 20 12*0 8 30
  //   8 20 12*0 8 30 14*0 8 30 14*0 8 30 14*0 8 30 14*0 8 30 14*0 8 30 14*0 8 30 14*0 8 30 14*0 8 30 14*0
  //   8 30 14*0 8 30 14*0 8 30 14*0 8 30 14*0 8 30 14*0 8 30 14*0 8 30 14*0 8 30 14*0 8 30 14*0 8 30 14*0
  //   8 30 14*0 8 30 14*0 8 30 14*0 8 30 14*0 8 30 14*0 8 30 14*0 8 30 14*0 8 30 14*0 8 30 14*0 8 30 14*0
  //   8 30 14*0 8 30 14*0 8 30 14*0 8 30 14*0 8 30 14*0 8 30 14*0 8 30 14*0 8 30 14*0 8 30 14*0 8 30 14*0
  //   8 30 14*0 8 30 14*0 8 30 14*0 8 30 14*0 8 30 14*0 8 30 14*0 8 30 14*0 8 30 14*0 8 30 14*0 8 30 14*0
  //   8 30 14*0 8 30 14*0 8 30 14*0 8 30 14*0 8 30 14*0 8 30 14*0 8 30 14*0 8 30 14*0 8 30 14*0 8 30 14*0
  //   8 30 14*0 8 30 14*0 8 30 14*0 8 30 14*0 8 30 14*0 8 30 14*0 8 30 14*0 8 30 14*0 8 30 14*0 8 30 14*0
  //   8 30 14*0 8 30 14*0 8 30 14*0 8 30 14*0 8 30 14*0 8 30 14*0 8 30 14*0 8 30 14*0 8 30 14*0 8 30 14*0
  //   8 30 14*0 8 30 14*0 8 30 14*0 8 30 14*0 8 30 14*0 8 30 14*0 8 30 14*0 8 30 14*0 8 30 14*0 8 30 14*0
  //   8 30 14*0 8 30 14*0 8 30 14*0 8 30 14*0 8 30 14*0 8 30 14*0 8 30 14*0 8 30 14*0 8 30 14*0 8 30 14*0
  //   8 30 14*0 8 30 14*0 8 30 14*0 8 30 14*0 8 30 14*0 8 30 14*0 8 30 14*0 8 30 14*0 8 30 14*0 8 30 14*0
  //   8 30 14*0 8 30 14*0 8 30 14*0 8 30 14*0 8 30 14*0 8 30 14*0 8 30 14*0 8 30 14*0 8 30 14*0 8 30 14*0
  //   8 30 14*0 8 30 14*0 8 30 14*0 8 30 14*0 8 30 14*0 8 30 14*0 8 30 14*0 8 30 14*0 8 30 14*0 8 30 14*0
  //   8 30 14*0 8 30 14*0 8 30 14*0 8 30 14*0 8 30 14*0 8 30 14*0 8 30 14*0 8 30 14*0 8 30 14*0 8 30 14*0
  //   8 30 14*0 8 30 14*0 8 30 14*0 8 30 14*0 8 30 14*0 8 30 14*0 8 30 14*0 8 30 14*0 8 30 14*0 8 30 14*0
  //   8 30 14*0 8 30 14*0 8 30 14*0 8 30 14*0 8 30 14*0 8 30 14*0 8 30 14*0 8 30 14*0 8 30 14*0 8 30 14*0
  //   8 30 14*0 8 30 14*0 8 30 14*0 8 30 14*0 8 30 14*0 8 30 14*0 8 30 14*0 8 30 14*0 8 30 14*0 8 30 14*0
  //   8 30 14*0 8 30 14*0 8 30 14*0 8 30 14*0 8 30 14*0 8 30 14*0 8 30 14*0 8 30 14*0 8 30 14*0 8 30 14*0
  //   8 30 14*0 8 30 14*0 8 30 14*0 8 30 14*0 8 30 14*0 8 30 14*0 8 30 14*0 8 30 14*0 8 30 14*0 8 30 14*0
  //   8 30 14*0 8 30 14*0 8 30 14*0 8 30 14*0 8 30 14*0 8 30 14*0 8 30 14*0 8 30 14*0 8 30 14*0 8 30 14*0
  //   8 30 14*0 8 30 14*0 8 30 14*0 8 30 14*0 8 30 14*0 8 30 14*0 8 30 14*0 8 30 14*0 8 30 14*0 8 30 14*0
  //   8 30 14*0 8 30 14*0 8 30 14*0 8 30 14*0 8 30 14*0 8 30 14*0 8 30 14*0 8 30 14*0 8 30 14*0 8 30 14*0
  //   8 30 14*0 8 30 14*0 8 30 14*0 8 30 14*0 8 30 14*0 8 30 14*0 8 30 14*0 8 30 14*0 8 30 14*0 8 30 14*0
  //   8 30 14*0 8 30 14*0 8 30 14*0 8 30 14*0 8 30 14*0 8 30 14*0 8 30 14*0 8 30 14*0 8 30 14*0 8 30 14*0
  //   8 30 14*0 8 30 14*0 8 30 14*0 8 30 14*0 8 30 14*0 8 30 14*0 8 30 14*0 8 30 14*0 8 30 14*0 8 30 14*0
  //   8 30 14*0 8 30 14*0 8 30 14*0 8 30 14*0 8 30 14*0 8 30 14*0 8 30 14*0 8 30 14*0 8 30 14*0 8 30 14*0
  //   8 30 14*0 8 30 14*0 8 30 14*0 8 30 14*0 8 30 14*0 8 30 14*0 8 30 14*0 8 30 14*0 8 30 14*0 8 30 14*0
  //   8 30 14*0 8 30 14*0 8 30 14*0 8 30 14*0 8 30 14*0 8 30 14*0 8 30 14*0 8 30 14*0 8 30 14*0 8 30 14*0
  //   8 30 14*0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
endmodule
